# Fritzing sketch Ultrasonic_Touch button (saved by Fritzing 0.9.0b)
circuit board: 16.9333cm x 5.64444cm
breadboards: 1

parts:
  Componente1 = Arduino Uno (Rev3)
  LED1 = LED - 5mm [color="Yellow (595nm)" package="5 mm [THT]"]
  R1 = Resistor [tolerance=±0.05% resistance=110 package=THT]
  U1 = HC-SR04 [chip_label=IC package="SIP (Single Inline) [THT]"]
  R2 = Resistor [tolerance=±0.05% resistance=330 package=THT]
  LED2 = LED - 5mm [color="Red (635nm)" package="5 mm [THT]"]
  R3 = Resistor [tolerance=±0.05% resistance=47k package=THT]
  S1 = Momentary Switch [package=ksa_sealed_tac_switch]

nets (from the breadboard view):
  N1: Componente1.D8, R1.Pin_1
  N2: Componente1.D9_PWM, R2.Pin_1
  N3: Componente1.D2, R3.Pin_1, S1.1, S1.3
  N4: Componente1.D4, R3.Pin_0
  N5: Componente1.D7, U1.SIG
  GND: Componente1.GND, LED1.cathode, U1.GND, LED2.cathode, S1.2, S1.4
  N6: LED1.anode, R1.Pin_0
  N7: R2.Pin_0, LED2.anode

custom parts:
  HC-SR04: HC-SR04 ultrasound distance sensor

// code stored in the sketch: XivelyClientString_temperature.ino


/*
  Xively sensor client with Strings
 
 This sketch connects an analog sensor to Xively (http://www.xively.com)
 using a Wiznet Ethernet shield. You can use the Arduino Ethernet shield, or
 the Adafruit Ethernet shield, either one will work, as long as it's got
 a Wiznet Ethernet module on board.
 
 This example has been updated to use version 2.0 of the xively.com API. 
 To make it work, create a feed with two datastreams, and give them the IDs
 sensor1 and sensor2. Or change the code below to match your feed.

 This example uses the String library, which is part of the Arduino core from
 version 0019.

 Circuit:
 * Analog sensor attached to analog in 0
 * Ethernet shield attached to pins 10, 11, 12, 13

 created 15 March 2010
 modified 9 Apr 2012
 by Tom Igoe with input from Usman Haque and Joe Saavedra
 modified 8 September 2012
 by Scott Fitzgerald
 
 http://arduino.cc/en/Tutorial/XivelyClientString
 This code is in the public domain.

 */

#include <SPI.h>
#include <Ethernet.h>

#include <dht11.h>
dht11 DHT;

#define APIKEY         "YfqMfUI4h9QIZ0dL8JQTpqfhIfaeXwGOc7qrpPeoFHecVPEI" // replace your Xively api key here
#define FEEDID         863324820 // replace your feed ID
#define USERAGENT      "make fair" // user agent is the project name

#define sonicPin 7
#define ledPin 8
#define tempPin 6
// assign a MAC address for the ethernet controller.
// fill in your address here:
byte mac[] = {
  0xDE, 0xAD, 0xBE, 0xEF, 0xFE, 0xED
};

// fill in an available IP address on your network here,
// for manual configuration:
IPAddress ip(192, 168, 122, 5);

// initialize the library instance:
EthernetClient client;

// if you don't want to use DNS (and reduce your sketch size)
// use the numeric IP instead of the name for the server:
//IPAddress server(216,52,233,121);      // numeric IP for api.xively.com
char server[] = "api.xively.com";   // name address for xively API

unsigned long lastConnectionTime = 0;          // last time you connected to the server, in milliseconds
boolean lastConnected = false;                 // state of the connection last time through the main loop
const unsigned long postingInterval = 4*1000;  //delay between updates to xively.com


long cmtomicro(long a){
  return a/29/2;
}
long inchtomicro(long b){
  return b/74/2;
}
int sonicval;

void setup() {
  // Open serial communications and wait for port to open:
  Serial.begin(9600);
  while (!Serial) {
    ; // wait for serial port to connect. Needed for Leonardo only
  }


  // give the ethernet module time to boot up:
  //delay(1000);
  // start the Ethernet connection:
  pinMode(sonicPin, OUTPUT);
  pinMode(ledPin,OUTPUT);
  digitalWrite(sonicPin, HIGH);// 소닉핀 초기화
  digitalWrite(ledPin, LOW);
  if (Ethernet.begin(mac) == 0) {
    Serial.println("Failed to configure Ethernet using DHCP");
    // DHCP failed, so use a fixed IP address:
    Ethernet.begin(mac, ip);
  }
  Serial.print("My IP address: ");
  ip = Ethernet.localIP();
  for (byte thisByte = 0; thisByte < 4; thisByte++) {
    // print the value of each byte of the IP address:
    Serial.print(ip[thisByte], DEC);
    Serial.print(".");
  }
  Serial.println();
}

void loop() {
  // read the analog sensor:

  // convert the data to a String to send it:

  // if there's incoming data from the net connection.
  // send it out the serial port.  This is for debugging
  // purposes only:
  if (client.available()) {
    char c = client.read();
    Serial.print(c);
 }

  // if there's no net connection, but there was one last time
  // through the loop, then stop the client:
  if (!client.connected() && lastConnected) {
    Serial.println();
    Serial.println("disconnecting.");
    client.stop();
  }


  // if you're not connected, and ten seconds have passed since
  // your last connection, then connect again and send data:
  if (!client.connected() && (millis() - lastConnectionTime > postingInterval)) 
  {
    digitalWrite(sonicPin,LOW);
    delayMicroseconds(2);
    digitalWrite(sonicPin,HIGH);
    delayMicroseconds(5);
    digitalWrite(sonicPin,LOW);
    pinMode(sonicPin, INPUT);
    digitalWrite(ledPin, LOW);
    sonicval = pulseIn(sonicPin,HIGH);//analogRead(A0);
    pinMode(sonicPin, OUTPUT);
    int ultra_sensorReading= cmtomicro(sonicval); // cm거리계산
    if(ultra_sensorReading<=10){
     digitalWrite(ledPin, HIGH);
    }
    String dataString = "Ultra,";
    dataString += ultra_sensorReading;
    
    int sensor_val = DHT.read(tempPin);
    int temp_SensorReading=  DHT.temperature;
   // float temp =  sensor_val* 5.0;
    //temp  /=1024;
//    float temp_SensorReading =  100*(temp-0.5);
  //  Serial.print("temp_SensorReading = ");
    //Serial.print(temp_SensorReading);
    dataString += "\nTemperature, ";
    dataString += temp_SensorReading;
  
    sendData(dataString);
  }
  // store the state of the connection for next time through
  // the loop:
  lastConnected = client.connected();
}

// this method makes a HTTP connection to the server:
void sendData(String thisData) {
  // if there's a successful connection:


  if (client.connect(server, 80)) {
    Serial.println("connecting...");
    // send the HTTP PUT request:
    client.print("PUT /v2/feeds/");
    client.print(FEEDID);
    client.println(".csv HTTP/1.1");
    client.println("Host: api.xively.com");
    client.print("X-ApiKey: ");
    client.println(APIKEY);
    client.print("User-Agent: ");
    client.println(USERAGENT);
    client.print("Content-Length: ");
    client.println(thisData.length());

    // last pieces of the HTTP PUT request:
    client.println("Content-Type: text/csv");
    client.println("Connection: close");
    client.println();

    // here's the actual content of the PUT request:
    client.println(thisData);
    client.println();
  }
  else {
    // if you couldn't make a connection:
    Serial.println("connection failed");
    Serial.println();
    Serial.println("disconnecting.");
    client.stop();
  }
  // note the time that the connection was made or attempted:
  lastConnectionTime = millis();
}
